# Fritzing sketch ESP-Arduino-Serial (saved by Fritzing 0.9.3b)

parts:
  Part1 = Arduino Mega ADK (Rev3)
  U1 = NodeMCU V1.0

nets:
  GND: Part1.GND, U1.GND
  N1: Part1.D11_PWM, U1.D7
  N2: Part1.D10_PWM, U1.D8

custom parts:
  NodeMCU V1.0: ESP8266 based NodeMCU
