# Fritzing sketch MayCuonDay2Truc (saved by Fritzing 0.9.3b)
breadboards: 1

parts:
  Part1 = Arduino Uno (Rev3) - ICSP
  M1 = Stepper Motor - Unipolar
  M2 = Stepper Motor - Unipolar
  B10k = Rotary Potentiometer (Small) [maximum_resistance=100kΩ package=THT]
  START = Pushbutton [package="[THT]"]
  PAUSE = Pushbutton [package="[THT]"]
  STOP = Pushbutton [package="[THT]"]

nets:
  N1: Part1.A0, STOP.Pin_1, STOP.Pin_2
  N2: Part1.A1, PAUSE.Pin_1, PAUSE.Pin_2
  N3: Part1.A2, START.Pin_1, START.Pin_2
  N4: Part1.A3, B10k.wiper
  N5: Part1.D2, M2.COMMON_2
  N6: Part1.D4, M1.COMMON_2
  N7: Part1.D5_PWM, M2.COMMON_1
  N8: Part1.D7, M1.COMMON_1
  N9: Part1.5V, B10k.leg1
  N10: Part1.GND, B10k.leg2, START.Pin_3, START.Pin_4, PAUSE.Pin_3, PAUSE.Pin_4, STOP.Pin_3, STOP.Pin_4

notes:
  Driver TB6600
  Dir A Pul A
  Driver TB6600
  Dir X Pul X
  Speed control B10K
