# Fritzing sketch baixe_v1 (saved by Fritzing 0.9.10b)

parts:
  Part1 = Arduino Nano (Rev3.0) (ICSP)
  J1 = Basic Servo
  J2 = Screw terminal - 2 pins [package=THT]
  J3 = Basic Servo  # not connected

nets:
  GND: Part1.GND, J1.gnd
  N1: Part1.D4, J1.pulse
  N2: J1.vcc, J2.pin1
