# Fritzing sketch ghost_trap (saved by Fritzing 0.9.3b)
breadboards: 1

parts:
  LED1 = smd LED [color="Red (633nm)" package="1206 [SMD]"]
  Part1 = Arduino Uno (Rev3) - ICSP
  R1 = Resistor [tolerance=±5% resistance=220 package="0603 [SMD]"]
  S2 = Round Pushbutton
  U1 = WS2812 RGB LED matrix 1x8
  Part3 = 12 NeoPixel Ring [part_number=1643]
  DFPlayer_Mini2 = DFPlayer MINI [package="DIP (Dual Inline) [THT]"]
  R2 = Resistor [tolerance=±5% resistance=220 package="0603 [SMD]"]
  SP1 = SPEAKER [package=pcb_mount_speaker]

nets:
  N1: LED1.cathode, R1.Pin_0
  N2: LED1.anode, Part1.D13/SCK
  VCC: Part1.5V, U1.VCC, Part3.VDD, DFPlayer_Mini2.VCC
  N3: Part1.D8, Part3.IN
  N4: Part1.D9_PWM, U1.DIN
  N5: Part1.D10_PWM/SS, DFPlayer_Mini2.TX
  N6: Part1.D11_PWM/MOSI, R2.Pin_1
  N7: Part1.D2, S2.leg0
  GND: Part1.GND, R1.Pin_1, S2.leg1, U1.GND, Part3.GND, DFPlayer_Mini2.GND#9
  N8: DFPlayer_Mini2.RX, R2.Pin_0
  N9: DFPlayer_Mini2.SPK1, SP1.-
  N10: DFPlayer_Mini2.SPK2, SP1.+

custom parts:
  WS2812 RGB LED matrix 1x8: WS2812 matrix 1x8
  12 NeoPixel Ring: 12 ultra bright smart LED NeoPixels are arranged in a circle with 1.5" (37mm) outer diameter. The rings are 'chainable' - connect the output pin of one to the input pin of another. Use only one microcontroller pin to control as many as you can chain together! Each LED is addressable as the driver chip is inside the LED. Each one has ~18mA constant current drive so the color will be very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
  DFPlayer MINI: MP3 module by DFRobot.com for playing Music from an SD-Card. Supports WAV and MP3 files.
